// Digital circuit Circuito final.dig as structural Verilog
module Circuito_final (
  input  Sign,
  output S0,
  output S1,
  output S2
);

  wire A0_out, A1_out, A2_out, B0_out, B1_out, B2_out, sumadorcompleto_1_cout, sumadorcompleto_2_cout,
       xor_1_out, xor_2_out, xor_3_out;

  DipSwitch A0 (.out(A0_out));
  DipSwitch A1 (.out(A1_out));
  DipSwitch A2 (.out(A2_out));
  DipSwitch B0 (.out(B0_out));
  DipSwitch B1 (.out(B1_out));
  DipSwitch B2 (.out(B2_out));
  xor xor_1 (xor_1_out, B0_out, Sign);
  xor xor_2 (xor_2_out, B1_out, Sign);
  xor xor_3 (xor_3_out, B2_out, Sign);
  SumadorCompleto sumadorcompleto_1 (.A(A0_out), .B(xor_1_out), .Cin(Sign), .Cout(sumadorcompleto_1_cout), .S(S0));
  SumadorCompleto sumadorcompleto_2 (
    .A(A1_out), .B(xor_2_out), .Cin(sumadorcompleto_1_cout), .Cout(sumadorcompleto_2_cout), .S(S1));
  SumadorCompleto sumadorcompleto_3 (.A(A2_out), .B(xor_3_out), .Cin(sumadorcompleto_2_cout), .S(S2));  // open: Cout
endmodule
